// Digital circuit drv16.dig as structural Verilog
// 16 bit processor which is compatible at the assembly language level with RISC-V
module drv16 (
  input  clock,
  input  reset,
  input  [15:0] dIn,
  output [14:0] addr,
  output wr,
  output [15:0] dOut,
  output rd
);

  wire [0:0] multiplexer_2_out;
  wire [15:0] bytes_1_tord, multiplexer_1_out, registerfile_1_da, registerfile_1_db, undriven;

  Multiplexer #(.Bits(16)) multiplexer_1 (.in_0(undriven), .in_1(bytes_1_tord), .out(multiplexer_1_out));  // open: sel
  RegisterFile #(.AddrBits(4), .Bits(16)) registerfile_1 (
    .Din(multiplexer_1_out), .C(clock), .Da(registerfile_1_da), .Db(registerfile_1_db));  // open: we, Rw, Ra, Rb
  alu alu_1 ();  // open: A, B, sub, logSelect, logic, R, NE, GE
  bytes bytes_1 (
    .dIn(dIn), .A0(multiplexer_2_out[0]), .fromRS2(registerfile_1_db), .dOut(dOut), .toRD(bytes_1_tord));  // open: sign, word
  Multiplexer #(.Bits(16)) multiplexer_2 (
    .in_0(undriven), .in_1(registerfile_1_da), .out({addr, multiplexer_2_out[0]}));  // open: sel

  assign rd = 1'b1;
  assign wr = reset;

  // Notes on the sheet:
  //   addr: selects a 16 bit word in memory to be read or changed
  //   wr: indicates a write operation
  //   dOut: word to be sent to memory
  //   reset: when high prepares the processor to execute from address 0
  //   dIn: word coming from memory
  //   rd: indicates that memory will be read in this cycle
endmodule
