// Digital circuit system.dig as structural Verilog
module system (
  input  clk
);

  wire and_1_out, comparator_1_eq, cpu_wr, reset_out;
  wire [14:0] cpu_addr;
  wire [15:0] cpu_dout, ramdualport_1_d;

  Button reset (.out(reset_out));
  drv16 cpu (
    .clock(clk), .reset(reset_out), .dIn(ramdualport_1_d), .addr(cpu_addr), .wr(cpu_wr), .dOut(cpu_dout));  // open: rd
  Comparator #(.Bits(15)) comparator_1 (.a({15{1'b1}}), .b(cpu_addr), .eq(comparator_1_eq));  // open: gt, lt
  RAMDualPort #(.AddrBits(15), .isProgramMemory("true"), .Bits(16)) ramdualport_1 (
    .A(cpu_addr), .Din(cpu_dout), .str(cpu_wr), .C(clk), .ld(1'b1), .D(ramdualport_1_d));
  and and_1 (and_1_out, comparator_1_eq, cpu_wr);
  Terminal terminal_1 (.D(cpu_dout), .C(clk), .en(and_1_out));
endmodule
